# Fritzing sketch schematic (saved by Fritzing 0.9.3b)
breadboards: 1

parts:
  U2 = NodeMCU V1.0
  RFID = RFID-RC522-v2

nets:
  N1: U2.D8, RFID.RST
  N2: U2.CLK, RFID.SCK
  N3: U2.SD0, RFID.MISO
  N4: U2.SD1, RFID.MOSI

custom parts:
  NodeMCU V1.0: ESP8266 based NodeMCU
  RFID-RC522-v2: A simple China made RFID-RC522 Reader; do check the pin labels, as this is a MFRC522 based clone.
